// Logisim project alu.circ as structural Verilog: 5 circuits, main circuit alu
module alu (
  input  [31:0] A,
  input  [31:0] B,
  input  [3:0] ALUSel,
  output [31:0] Result
);

  wire comparator_1_lt, comparator_2_lt;
  wire [31:0] add, alu_sll, switch0, switch1, switch2, switch3, switch4, switch5, switch6, switch7, switch8,
       switch9, switch10, switch11, switch12, switch13, switch14, switch15, switch16, switch17;

  assign switch0 = A & B;  // AND_Gate and_1, 32 bits wide
  assign switch1 = A | B;  // OR_Gate or_1, 32 bits wide
  Adder #(.width(32)) adder_1 (.a(A), .b(B), .out(switch3));  // open: cin, cout
  Subtractor #(.width(32)) subtractor_1 (.a(A), .b(B), .out(switch4));  // open: bin, bout
  Multiplier #(.width(32)) multiplier_1 (.a(A), .b(B), .out(switch5), .cout(switch6));  // open: cin
  assign switch2 = A ^ B;  // XOR_Gate xor_1, 32 bits wide
  Adder #(.width(32)) adder_2 (.a(A), .b(B), .out(add));  // open: cin, cout
  mult mult_1 (.in_1(A), .in_2(B), .out_3(switch7));
  Divider #(.width(32)) divider_1 (.a(A), .b(B), .out(switch8));  // open: upper, rem
  divu divu_1 (.in_1(A), .in_2(B), .out_3(switch9));
  Divider #(.width(32)) divider_2 (.a(A), .b(B), .rem(switch10));  // open: out, upper
  Shifter #(.width(32)) shifter_1 (.in(A), .\dist (B[4:0]), .out(switch16));
  Comparator #(.width(32)) comparator_1 (.a(A), .b(B), .lt(comparator_1_lt));  // open: gt, eq
  Shifter #(.width(32), .shift("lr")) shifter_2 (.in(A), .\dist (B[4:0]), .out(switch11));
  Shifter #(.width(32), .shift("ar")) shifter_3 (.in(A), .\dist (B[4:0]), .out(switch12));
  Comparator #(.width(32)) comparator_2 (.a(A), .b(B), .lt(comparator_2_lt));  // open: gt, eq
  assign switch17 = {{31{1'b0}}, comparator_1_lt};  // Bit_Extender bit_extender_1
  assign switch13 = {{31{1'b0}}, comparator_2_lt};  // Bit_Extender bit_extender_2
  Multiplexer #(.select(4), .width(32), .enable("false")) multiplexer_1 (
    .in0(add), .in1(switch0), .in2(switch1), .in3(switch2), .in4(switch11), .in5(switch12), .in6(alu_sll),
    .in7(switch17), .in8(switch8), .in9(switch10), .in10(switch5), .in11(switch6), .in12(switch4),
    .in13(switch9), .in14(switch7), .in15(B), .out(Result), .sel(ALUSel));
  Shifter #(.width(32)) shifter_4 (.in(A), .\dist (B[4:0]), .out(alu_sll));
  sir sir_1 (.in_1(A), .in_2(B), .out_3(switch14));
  cnto cnto_1 (.in_1(A), .in_2(B), .out_3(switch15));

  // Other names for the same wires on the sheet: switch20[31:0] = B

  // Notes on the sheet:
  //   INPUTS to your circuit
  //   DON'T CHANGE THE LOCATIONS OF THE INPUTS AND OUTPUTS!
  //   OUTPUT from your circuit
endmodule

module mult (
  input  [31:0] in_1,
  input  [31:0] in_2,
  output [31:0] out_3
);

  wire adder_1_cout, xor_1_out, xor_2_out, xor_3_out;
  wire [31:0] adder_2_out, bit_extender_1_out, multiplexer_1_out, multiplexer_2_out, multiplier_1_cout,
       multiplier_1_out, negator_1_out, negator_2_out, subtractor_1_out, subtractor_2_out;

  Negator #(.width(32)) negator_1 (.in(in_1), .out(negator_1_out));
  Negator #(.width(32)) negator_2 (.in(in_2), .out(negator_2_out));
  xor xor_1 (xor_1_out, in_1[31], 1'b0);
  xor xor_2 (xor_2_out, in_2[31], 1'b0);
  Multiplexer #(.width(32), .enable("false")) multiplexer_1 (
    .in0(in_1), .in1(negator_1_out), .out(multiplexer_1_out), .sel(xor_1_out));
  Multiplexer #(.width(32), .enable("false")) multiplexer_2 (
    .in0(in_2), .in1(negator_2_out), .out(multiplexer_2_out), .sel(xor_2_out));
  xor xor_3 (xor_3_out, xor_1_out, xor_2_out);
  Subtractor #(.width(32)) subtractor_1 (
    .a({32{1'b1}}), .b(multiplier_1_out), .out(subtractor_1_out));  // open: bin, bout
  Adder #(.width(32)) adder_1 (.a(subtractor_1_out), .b(32'h1), .cout(adder_1_cout));  // open: out, cin
  Multiplier #(.width(32)) multiplier_1 (
    .a(multiplexer_1_out), .b(multiplexer_2_out), .out(multiplier_1_out), .cout(multiplier_1_cout));  // open: cin
  Subtractor #(.width(32)) subtractor_2 (
    .a({32{1'b1}}), .b(multiplier_1_cout), .out(subtractor_2_out));  // open: bin, bout
  assign bit_extender_1_out = {{31{1'b0}}, adder_1_cout};  // Bit_Extender bit_extender_1
  Adder #(.width(32)) adder_2 (.a(subtractor_2_out), .b(bit_extender_1_out), .out(adder_2_out));  // open: cin, cout
  Multiplexer #(.width(32), .enable("false")) multiplexer_3 (
    .in0(multiplier_1_cout), .in1(adder_2_out), .out(out_3), .sel(xor_3_out));
endmodule

module divu (
  input  [31:0] in_1,
  input  [31:0] in_2,
  output [31:0] out_3
);

  wire xor_1_out, xor_2_out, xor_3_out;
  wire [31:0] divider_1_out, multiplexer_1_out, multiplexer_2_out, negator_1_out, negator_2_out,
       negator_3_out;

  Negator #(.width(32)) negator_1 (.in(in_1), .out(negator_1_out));
  Negator #(.width(32)) negator_2 (.in(in_2), .out(negator_2_out));
  xor xor_1 (xor_1_out, in_1[31], 1'b0);
  xor xor_2 (xor_2_out, in_2[31], 1'b0);
  Multiplexer #(.width(32), .enable("false")) multiplexer_1 (
    .in0(in_1), .in1(negator_1_out), .out(multiplexer_1_out), .sel(xor_1_out));
  Multiplexer #(.width(32), .enable("false")) multiplexer_2 (
    .in0(in_2), .in1(negator_2_out), .out(multiplexer_2_out), .sel(xor_2_out));
  xor xor_3 (xor_3_out, xor_1_out, xor_2_out);
  Divider #(.width(32)) divider_1 (
    .a(multiplexer_1_out), .b(multiplexer_2_out), .out(divider_1_out));  // open: upper, rem
  Negator #(.width(32)) negator_3 (.in(divider_1_out), .out(negator_3_out));
  Multiplexer #(.width(32), .enable("false")) multiplexer_3 (
    .in0(divider_1_out), .in1(negator_3_out), .out(out_3), .sel(xor_3_out));
endmodule

module sir (
  input  [31:0] in_1,
  input  [31:0] in_2,
  output [31:0] out_3
);

  wire comparator_1_eq;

  Comparator #(.width(32)) comparator_1 (
    .a(in_1),
    .b({in_2[0], in_2[1], in_2[2], in_2[3], in_2[4], in_2[5], in_2[6], in_2[7], in_2[8], in_2[9], in_2[10], in_2[11], in_2[12], in_2[13], in_2[14], in_2[15], in_2[16], in_2[17], in_2[18], in_2[19], in_2[20], in_2[21], in_2[22], in_2[23], in_2[24], in_2[25], in_2[26], in_2[27], in_2[28], in_2[29], in_2[30], in_2[31]}),
    .eq(comparator_1_eq));  // open: gt, lt
  assign out_3 = {{31{1'b0}}, comparator_1_eq};  // Bit_Extender bit_extender_1
endmodule

module cnto (
  input  [31:0] in_1,
  input  [31:0] in_2,
  output [31:0] out_3
);

  wire [5:0] bitadder_1_out, bitadder_2_out;
  wire [31:0] bit_extender_1_out, bit_extender_2_out;

  BitAdder #(.width(32)) bitadder_1 (.in0(in_1), .out(bitadder_1_out));
  BitAdder #(.width(32)) bitadder_2 (.in0(in_2), .out(bitadder_2_out));
  assign bit_extender_1_out = {{26{1'b0}}, bitadder_1_out};  // Bit_Extender bit_extender_1
  assign bit_extender_2_out = {{26{1'b0}}, bitadder_2_out};  // Bit_Extender bit_extender_2
  Adder #(.width(32)) adder_1 (.a(bit_extender_1_out), .b(bit_extender_2_out), .out(out_3));  // open: cin, cout
endmodule
