// Logisim project regfile.circ as structural Verilog: 4 circuits, main circuit main
module main (
  input  [4:0] rs1,
  input  [4:0] rs2,
  input  [4:0] rd,
  input  [31:0] Write_Data,
  input  RegWEn,
  input  clk,
  output [31:0] Read_Data_1,
  output [31:0] ra,
  output [31:0] sp,
  output [31:0] t0,
  output [31:0] t1,
  output [31:0] t2,
  output [31:0] s0,
  output [31:0] s1,
  output [31:0] a0,
  output [31:0] Read_Data_2
);

  wire demultiplexer_1_out1, demultiplexer_1_out2, demultiplexer_1_out5, demultiplexer_1_out6,
       demultiplexer_1_out7, demultiplexer_1_out8, demultiplexer_1_out9, demultiplexer_1_out10;
  wire [3:0] multiplexer_1_out, multiplexer_2_out;
  wire [31:0] demultiplexer_2_out1, demultiplexer_2_out2, demultiplexer_2_out5, demultiplexer_2_out6,
       demultiplexer_2_out7, demultiplexer_2_out8, demultiplexer_2_out9, demultiplexer_2_out10;

  Demultiplexer #(.select(4), .enable("false")) demultiplexer_1 (
    .out1(demultiplexer_1_out1), .out2(demultiplexer_1_out2), .out5(demultiplexer_1_out5),
    .out6(demultiplexer_1_out6), .out7(demultiplexer_1_out7), .out8(demultiplexer_1_out8),
    .out9(demultiplexer_1_out9), .out10(demultiplexer_1_out10), .in(1'b1), .sel(multiplexer_1_out));  // open: out0, out3, out4, out11, out12, out13, out14, out15
  Multiplexer #(.width(4), .enable("false")) multiplexer_1 (
    .in0(4'b0000), .in1(rd[3:0]), .out(multiplexer_1_out), .sel(RegWEn));
  Multiplexer #(.width(4), .enable("false")) multiplexer_2 (
    .in0(4'b0000), .in1(rd[3:0]), .out(multiplexer_2_out), .sel(RegWEn));
  Demultiplexer #(.select(4), .width(32), .enable("false")) demultiplexer_2 (
    .out1(demultiplexer_2_out1), .out2(demultiplexer_2_out2), .out5(demultiplexer_2_out5),
    .out6(demultiplexer_2_out6), .out7(demultiplexer_2_out7), .out8(demultiplexer_2_out8),
    .out9(demultiplexer_2_out9), .out10(demultiplexer_2_out10), .in(Write_Data), .sel(multiplexer_2_out));  // open: out0, out3, out4, out11, out12, out13, out14, out15
  Register #(.width(32)) register_1 (
    .D(demultiplexer_2_out10), .en(demultiplexer_1_out10), .clk(clk), .Q(a0));  // open: clr
  Register #(.width(32)) register_2 (
    .D(demultiplexer_2_out1), .en(demultiplexer_1_out1), .clk(clk), .Q(ra));  // open: clr
  Register #(.width(32)) register_3 (
    .D(demultiplexer_2_out2), .en(demultiplexer_1_out2), .clk(clk), .Q(sp));  // open: clr
  Register #(.width(32)) register_4 (
    .D(demultiplexer_2_out5), .en(demultiplexer_1_out5), .clk(clk), .Q(t0));  // open: clr
  Register #(.width(32)) register_5 (
    .D(demultiplexer_2_out7), .en(demultiplexer_1_out7), .clk(clk), .Q(t2));  // open: clr
  Register #(.width(32)) register_6 (
    .D(demultiplexer_2_out8), .en(demultiplexer_1_out8), .clk(clk), .Q(s0));  // open: clr
  Register #(.width(32)) register_7 (
    .D(demultiplexer_2_out6), .en(demultiplexer_1_out6), .clk(clk), .Q(t1));  // open: clr
  Register #(.width(32)) register_8 (
    .D(demultiplexer_2_out9), .en(demultiplexer_1_out9), .clk(clk), .Q(s1));  // open: clr
  Multiplexer #(.select(4), .width(32), .enable("false")) multiplexer_3 (
    .in0({32{1'b0}}), .in1(ra), .in2(sp), .in3({32{1'b0}}), .in4({32{1'b0}}), .in5(t0), .in6(t1), .in7(t2),
    .in8(s0), .in9(s1), .in10(a0), .in11({32{1'b0}}), .in12({32{1'b0}}), .in13({32{1'b0}}),
    .in14({32{1'b0}}), .in15({32{1'b0}}), .out(Read_Data_1), .sel(rs1[3:0]));
  Multiplexer #(.select(4), .width(32), .enable("false")) multiplexer_4 (
    .in0({32{1'b0}}), .in1(ra), .in2(sp), .in3({32{1'b0}}), .in4({32{1'b0}}), .in5(t0), .in6(t1), .in7(t2),
    .in8(s0), .in9(s1), .in10(a0), .in11({32{1'b0}}), .in12({32{1'b0}}), .in13({32{1'b0}}),
    .in14({32{1'b0}}), .in15({32{1'b0}}), .out(Read_Data_2), .sel(rs2[3:0]));

  // Other names for the same wires on the sheet: read_data1[31:0] = Read_Data_1; read_data2[31:0] = Read_Data_2;
  //   read_reg1[4:0] = rs1; read_reg2[4:0] = rs2; write_en = RegWEn; write_reg[4:0] = rd

  // Notes on the sheet:
  //   INPUTS to your circuit
  //   DON'T CHANGE THE LOCATIONS OF THE INPUTS AND OUTPUTS!
  //   These are DEBUG/TEST outputs from your circuit.
  //   OUTPUTS from your circuit
endmodule

module test (
);

  wire clk, write_en;
  wire [3:0] multiplexer_1_out, multiplexer_2_out, read_reg1, write_reg;
  wire [31:0] a0, demultiplexer_1_out1, demultiplexer_1_out2, demultiplexer_1_out3, demultiplexer_1_out4,
       demultiplexer_1_out5, demultiplexer_1_out6, demultiplexer_1_out7, demultiplexer_1_out8,
       multiplexer_3_out, ra, read_data1, register_9_q, s0, s1, sp, t0, t1, t2, write_data, x0;

  Demultiplexer #(.select(4), .width(32), .enable("false")) demultiplexer_1 (
    .out1(demultiplexer_1_out1), .out2(demultiplexer_1_out2), .out3(demultiplexer_1_out3),
    .out4(demultiplexer_1_out4), .out5(demultiplexer_1_out5), .out6(demultiplexer_1_out6),
    .out7(demultiplexer_1_out7), .out8(demultiplexer_1_out8), .in(write_data), .sel(multiplexer_1_out));  // open: out0, out9, out10, out11, out12, out13, out14, out15
  Multiplexer #(.width(4), .enable("false")) multiplexer_1 (
    .in0(4'b0000), .in1(write_reg), .out(multiplexer_1_out), .sel(write_en));
  Register #(.width(32)) register_1 (.D(demultiplexer_1_out8), .clk(clk), .Q(a0));  // open: en, clr
  Register #(.width(32)) register_2 (.D(demultiplexer_1_out1), .clk(clk), .Q(ra));  // open: en, clr
  Register #(.width(32)) register_3 (.D(demultiplexer_1_out3), .clk(clk), .Q(t0));  // open: en, clr
  Register #(.width(32)) register_4 (.D(demultiplexer_1_out2), .clk(clk), .Q(sp));  // open: en, clr
  Register #(.width(32)) register_5 (.D(demultiplexer_1_out4), .clk(clk), .Q(t1));  // open: en, clr
  Register #(.width(32)) register_6 (.D(demultiplexer_1_out5), .clk(clk), .Q(t2));  // open: en, clr
  Register #(.width(32)) register_7 (.D(demultiplexer_1_out6), .clk(clk), .Q(s0));  // open: en, clr
  Register #(.width(32)) register_8 (.D(demultiplexer_1_out7), .clk(clk), .Q(s1));  // open: en, clr
  Register #(.width(32)) register_9 (.D(write_data), .clk(clk), .Q(register_9_q));  // open: en, clr
  Demultiplexer #(.select(4), .width(32), .enable("false")) demultiplexer_2 (
    .out1(ra), .out2(sp), .out3(t0), .out4(t1), .out5(t2), .out6(s0), .out7(s1), .out8(a0),
    .in(register_9_q), .sel(multiplexer_2_out));  // open: out0, out9, out10, out11, out12, out13, out14, out15
  Multiplexer #(.width(4), .enable("false")) multiplexer_2 (
    .in0(4'b0000), .in1(write_reg), .out(multiplexer_2_out), .sel(write_en));
  Register #(.width(32)) register_10 (.D(multiplexer_3_out), .clk(clk), .Q(read_data1));  // open: en, clr
  Multiplexer #(.select(4), .width(32), .enable("false")) multiplexer_3 (
    .in0(x0), .in1(ra), .in2(sp), .in3(t0), .in4(t1), .in5(t2), .in6(s0), .in7(s1), .in8(a0), .in9(x0),
    .in10(x0), .in11(x0), .in12(x0), .in13(x0), .in14(x0), .in15(x0), .out(multiplexer_3_out), .sel(read_reg1));
endmodule

module test2 (
  input  in_1
);

  wire clk, demultiplexer_2_out1, demultiplexer_2_out2, demultiplexer_2_out3, demultiplexer_2_out4,
       demultiplexer_2_out5, demultiplexer_2_out6, demultiplexer_2_out7, demultiplexer_2_out8, undriven,
       write_en;
  wire [3:0] multiplexer_1_out, multiplexer_10_out, write_reg;
  wire [31:0] a0, a0_1, adder_1_out, adder_2_out, adder_3_out, adder_4_out, adder_5_out, adder_6_out,
       adder_7_out, adder_8_out, multiplexer_2_out, multiplexer_3_out, multiplexer_4_out, multiplexer_5_out,
       multiplexer_6_out, multiplexer_7_out, multiplexer_8_out, multiplexer_9_out, ra, ra_1, s0, s0_1, s1,
       s1_1, sp, sp_1, t0, t0_1, t1, t1_1, t2, t2_1, write_data;

  Demultiplexer #(.select(4), .width(32), .enable("false")) demultiplexer_1 (
    .out1(ra_1), .out2(sp_1), .out3(t0_1), .out4(t1_1), .out5(t2_1), .out6(s0_1), .out7(s1_1), .out8(a0_1),
    .in(write_data), .sel(multiplexer_1_out));  // open: out0, out9, out10, out11, out12, out13, out14, out15
  Multiplexer #(.width(4), .enable("false")) multiplexer_1 (
    .in0(4'b0000), .in1(write_reg), .out(multiplexer_1_out), .sel(write_en));
  Adder #(.width(32)) adder_1 (.a(t1), .b(t1_1), .out(adder_1_out));  // open: cin, cout
  Adder #(.width(32)) adder_2 (.a(a0), .b(a0_1), .out(adder_2_out));  // open: cin, cout
  Adder #(.width(32)) adder_3 (.a(t0), .b(t0_1), .out(adder_3_out));  // open: cin, cout
  Multiplexer #(.width(32), .enable("false")) multiplexer_2 (
    .in0(adder_1_out), .in1(t1_1), .out(multiplexer_2_out), .sel(demultiplexer_2_out4));
  Adder #(.width(32)) adder_4 (.a(s1), .b(s1_1), .out(adder_4_out));  // open: cin, cout
  Multiplexer #(.width(32), .enable("false")) multiplexer_3 (
    .in0(adder_2_out), .in1(a0_1), .out(multiplexer_3_out), .sel(demultiplexer_2_out8));
  Adder #(.width(32)) adder_5 (.a(ra), .b(ra_1), .out(adder_5_out));  // open: cin, cout
  Adder #(.width(32)) adder_6 (.a(sp), .b(sp_1), .out(adder_6_out));  // open: cin, cout
  Register #(.width(32)) register_1 (.D(multiplexer_2_out), .clk(clk), .Q(t1));  // open: en, clr
  Adder #(.width(32)) adder_7 (.a(t2), .b(t2_1), .out(adder_7_out));  // open: cin, cout
  Adder #(.width(32)) adder_8 (.a(s0), .b(s0_1), .out(adder_8_out));  // open: cin, cout
  Multiplexer #(.width(32), .enable("false")) multiplexer_4 (
    .in0(adder_5_out), .in1(ra_1), .out(multiplexer_4_out), .sel(demultiplexer_2_out1));
  Multiplexer #(.width(32), .enable("false")) multiplexer_5 (
    .in0(adder_6_out), .in1(sp_1), .out(multiplexer_5_out), .sel(demultiplexer_2_out2));
  Multiplexer #(.width(32), .enable("false")) multiplexer_6 (
    .in0(adder_3_out), .in1(t0_1), .out(multiplexer_6_out), .sel(demultiplexer_2_out3));
  Multiplexer #(.width(32), .enable("false")) multiplexer_7 (
    .in0(adder_7_out), .in1(t2_1), .out(multiplexer_7_out), .sel(demultiplexer_2_out5));
  Multiplexer #(.width(32), .enable("false")) multiplexer_8 (
    .in0(adder_8_out), .in1(s0_1), .out(multiplexer_8_out), .sel(demultiplexer_2_out6));
  Multiplexer #(.width(32), .enable("false")) multiplexer_9 (
    .in0(adder_4_out), .in1(s1_1), .out(multiplexer_9_out), .sel(demultiplexer_2_out7));
  Register #(.width(32)) register_2 (.D(multiplexer_3_out), .clk(clk), .Q(a0));  // open: en, clr
  Register #(.width(32)) register_3 (.D(multiplexer_4_out), .clk(clk), .Q(ra));  // open: en, clr
  Register #(.width(32)) register_4 (.D(multiplexer_5_out), .clk(clk), .Q(sp));  // open: en, clr
  Register #(.width(32)) register_5 (.D(multiplexer_6_out), .clk(clk), .Q(t0));  // open: en, clr
  Register #(.width(32)) register_6 (.D(multiplexer_7_out), .clk(clk), .Q(t2));  // open: en, clr
  Register #(.width(32)) register_7 (.D(multiplexer_8_out), .clk(clk), .Q(s0));  // open: en, clr
  Register #(.width(32)) register_8 (.D(multiplexer_9_out), .clk(clk), .Q(s1));  // open: en, clr
  Multiplexer #(.width(4), .enable("false")) multiplexer_10 (
    .in0(4'b0000), .in1(write_reg), .out(multiplexer_10_out), .sel(write_en));
  Demultiplexer #(.select(4), .tristate("true"), .disabled("Z"), .enable("false")) demultiplexer_2 (
    .out1(demultiplexer_2_out1), .out2(demultiplexer_2_out2), .out3(demultiplexer_2_out3),
    .out4(demultiplexer_2_out4), .out5(demultiplexer_2_out5), .out6(demultiplexer_2_out6),
    .out7(demultiplexer_2_out7), .out8(demultiplexer_2_out8), .in(undriven), .sel(multiplexer_10_out));  // open: out0, out9, out10, out11, out12, out13, out14, out15
endmodule

module test_3 (
);

  wire clk;
  wire [3:0] read_reg1, read_reg2;
  wire [31:0] a0, ra, read_data1, read_data2, register_1_q, register_2_q, register_3_q, register_4_q,
       register_5_q, register_6_q, register_7_q, register_8_q, register_9_q, register_10_q, register_11_q,
       register_12_q, register_13_q, register_14_q, register_15_q, register_16_q, register_17_q,
       register_18_q, register_19_q, register_20_q, register_21_q, register_22_q, register_23_q,
       register_24_q, register_25_q, register_26_q, register_27_q, register_28_q, register_29_q,
       register_30_q, register_31_q, register_32_q, register_33_q, register_34_q, register_35_q,
       register_36_q, register_37_q, register_38_q, register_39_q, register_40_q, s0, s1, sp, t0, t1, t2, x0;

  Register #(.width(32)) register_1 (.D(s1), .clk(clk), .Q(register_1_q));  // open: en, clr
  Register #(.width(32)) register_2 (.D(t0), .clk(clk), .Q(register_2_q));  // open: en, clr
  Register #(.width(32)) register_3 (.D(s0), .clk(clk), .Q(register_3_q));  // open: en, clr
  Register #(.width(32)) register_4 (.D(sp), .clk(clk), .Q(register_4_q));  // open: en, clr
  Register #(.width(32)) register_5 (.D(x0), .clk(clk), .Q(register_5_q));  // open: en, clr
  Register #(.width(32)) register_6 (.D(ra), .clk(clk), .Q(register_6_q));  // open: en, clr
  Register #(.width(32)) register_7 (.D(t1), .clk(clk), .Q(register_7_q));  // open: en, clr
  Register #(.width(32)) register_8 (.D(t2), .clk(clk), .Q(register_8_q));  // open: en, clr
  Register #(.width(32)) register_9 (.D(x0), .clk(clk), .Q(register_9_q));  // open: en, clr
  Register #(.width(32)) register_10 (.D(a0), .clk(clk), .Q(register_10_q));  // open: en, clr
  Register #(.width(32)) register_11 (.D(s1), .clk(clk), .Q(register_11_q));  // open: en, clr
  Multiplexer #(.select(4), .width(32), .enable("false")) multiplexer_1 (
    .in0(register_9_q), .in1(register_6_q), .in2(register_4_q), .in3(register_2_q), .in4(register_7_q),
    .in5(register_8_q), .in6(register_3_q), .in7(register_1_q), .in8(register_10_q), .in9(register_5_q),
    .in10(register_5_q), .in11(register_5_q), .in12(register_5_q), .in13(register_5_q), .in14(register_5_q),
    .in15(register_5_q), .out(read_data1), .sel(read_reg1));
  Register #(.width(32)) register_12 (.D(t0), .clk(clk), .Q(register_12_q));  // open: en, clr
  Register #(.width(32)) register_13 (.D(s0), .clk(clk), .Q(register_13_q));  // open: en, clr
  Register #(.width(32)) register_14 (.D(sp), .clk(clk), .Q(register_14_q));  // open: en, clr
  Register #(.width(32)) register_15 (.D(x0), .clk(clk), .Q(register_15_q));  // open: en, clr
  Register #(.width(32)) register_16 (.D(ra), .clk(clk), .Q(register_16_q));  // open: en, clr
  Register #(.width(32)) register_17 (.D(t1), .clk(clk), .Q(register_17_q));  // open: en, clr
  Register #(.width(32)) register_18 (.D(t2), .clk(clk), .Q(register_18_q));  // open: en, clr
  Register #(.width(32)) register_19 (.D(x0), .clk(clk), .Q(register_19_q));  // open: en, clr
  Register #(.width(32)) register_20 (.D(a0), .clk(clk), .Q(register_20_q));  // open: en, clr
  Register #(.width(32)) register_21 (.D(t0), .clk(clk), .Q(register_21_q));  // open: en, clr
  Register #(.width(32)) register_22 (.D(s0), .clk(clk), .Q(register_22_q));  // open: en, clr
  Register #(.width(32)) register_23 (.D(s1), .clk(clk), .Q(register_23_q));  // open: en, clr
  Register #(.width(32)) register_24 (.D(sp), .clk(clk), .Q(register_24_q));  // open: en, clr
  Register #(.width(32)) register_25 (.D(x0), .clk(clk), .Q(register_25_q));  // open: en, clr
  Register #(.width(32)) register_26 (.D(t1), .clk(clk), .Q(register_26_q));  // open: en, clr
  Register #(.width(32)) register_27 (.D(t2), .clk(clk), .Q(register_27_q));  // open: en, clr
  Register #(.width(32)) register_28 (.D(x0), .clk(clk), .Q(register_28_q));  // open: en, clr
  Register #(.width(32)) register_29 (.D(ra), .clk(clk), .Q(register_29_q));  // open: en, clr
  Register #(.width(32)) register_30 (.D(a0), .clk(clk), .Q(register_30_q));  // open: en, clr
  Multiplexer #(.select(4), .width(32), .enable("false")) multiplexer_2 (
    .in0(register_19_q), .in1(register_16_q), .in2(register_14_q), .in3(register_15_q), .in4(register_15_q),
    .in5(register_12_q), .in6(register_17_q), .in7(register_18_q), .in8(register_13_q), .in9(register_11_q),
    .in10(register_20_q), .in11(register_15_q), .in12(register_15_q), .in13(register_15_q),
    .in14(register_15_q), .in15(register_15_q), .out(read_data1), .sel(read_reg1));
  Multiplexer #(.select(4), .width(32), .enable("false")) multiplexer_3 (
    .in0(register_28_q), .in1(register_29_q), .in2(register_24_q), .in3(register_21_q), .in4(register_26_q),
    .in5(register_27_q), .in6(register_22_q), .in7(register_23_q), .in8(register_30_q), .in9(register_25_q),
    .in10(register_25_q), .in11(register_25_q), .in12(register_25_q), .in13(register_25_q),
    .in14(register_25_q), .in15(register_25_q), .out(read_data2), .sel(read_reg2));
  Register #(.width(32)) register_31 (.D(t0), .clk(clk), .Q(register_31_q));  // open: en, clr
  Register #(.width(32)) register_32 (.D(s0), .clk(clk), .Q(register_32_q));  // open: en, clr
  Register #(.width(32)) register_33 (.D(s1), .clk(clk), .Q(register_33_q));  // open: en, clr
  Register #(.width(32)) register_34 (.D(sp), .clk(clk), .Q(register_34_q));  // open: en, clr
  Register #(.width(32)) register_35 (.D(x0), .clk(clk), .Q(register_35_q));  // open: en, clr
  Register #(.width(32)) register_36 (.D(ra), .clk(clk), .Q(register_36_q));  // open: en, clr
  Register #(.width(32)) register_37 (.D(t1), .clk(clk), .Q(register_37_q));  // open: en, clr
  Register #(.width(32)) register_38 (.D(t2), .clk(clk), .Q(register_38_q));  // open: en, clr
  Register #(.width(32)) register_39 (.D(x0), .clk(clk), .Q(register_39_q));  // open: en, clr
  Register #(.width(32)) register_40 (.D(a0), .clk(clk), .Q(register_40_q));  // open: en, clr
  Multiplexer #(.select(4), .width(32), .enable("false")) multiplexer_4 (
    .in0(register_39_q), .in1(register_36_q), .in2(register_34_q), .in3(register_35_q), .in4(register_35_q),
    .in5(register_31_q), .in6(register_37_q), .in7(register_38_q), .in8(register_32_q), .in9(register_33_q),
    .in10(register_40_q), .in11(register_35_q), .in12(register_35_q), .in13(register_35_q),
    .in14(register_35_q), .in15(register_35_q), .out(read_data2), .sel(read_reg2));
endmodule
