// Logisim project cpu.circ as structural Verilog: 4 circuits, main circuit main
module main (
  input  [31:0] INSTRUCTION,
  input  CLOCK,
  output [31:0] FETCH_ADDRESS,
  output [31:0] ra,
  output [31:0] sp,
  output [31:0] t0,
  output [31:0] t1,
  output [31:0] t2,
  output [31:0] s0,
  output [31:0] s1,
  output [31:0] a0
);

  wire ASel, BEQ, BLT, BrUn, BSel, MemRW, pcselect, RegWEn;
  wire [1:0] WBSel;
  wire [2:0] data_size, Immsel;
  wire [3:0] ALUSel;
  wire [31:0] adder_1_out, adder_2_out, alu_1_result, bit_extender_1_out, bit_extender_2_out,
       bit_extender_3_out, bit_extender_4_out, divider_1_out, imm_1_imm, instr, load_data, load_done,
       main_1_read_data_1, main_1_read_data_2, multiplexer_1_out, multiplexer_2_out, multiplexer_3_out,
       multiplexer_4_out, multiplexer_6_out, multiplier_1_out, register_2_q;

  Adder #(.width(32)) adder_1 (.a(FETCH_ADDRESS), .b(32'h1), .out(adder_1_out));  // open: cin, cout
  Multiplexer #(.width(32), .enable("false")) multiplexer_1 (
    .in0(adder_1_out), .in1(divider_1_out), .out(multiplexer_1_out), .sel(pcselect));
  Divider #(.width(32)) divider_1 (.a(alu_1_result), .b(32'h4), .out(divider_1_out));  // open: upper, rem
  Register #(.width(32)) register_1 (.D(multiplexer_1_out), .clk(CLOCK), .Q(FETCH_ADDRESS));  // open: en, clr
  Register #(.width(32)) register_2 (.D(FETCH_ADDRESS), .clk(CLOCK), .Q(register_2_q));  // open: en, clr
  Control control_1 (
    .in_1(instr), .BrEq(BEQ), .BrLT(BLT), .ImmSel(Immsel), .BrUn(BrUn), .Asel(ASel), .Bsel(BSel),
    .ALUSel(ALUSel), .MemRW(MemRW), .RegWEn(RegWEn), .WBSel(WBSel), .PCSel(pcselect), .data_size(data_size));
  Adder #(.width(32)) adder_2 (.a(register_2_q), .b(32'h4), .out(adder_2_out));  // open: cin, cout
  Register #(.width(32)) register_3 (.D(multiplexer_2_out), .clk(CLOCK), .Q(instr));  // open: en, clr
  Multiplexer #(.width(32), .enable("false")) multiplexer_2 (
    .in0(INSTRUCTION), .in1(32'h13), .out(multiplexer_2_out), .sel(pcselect));
  Imm imm_1 (.instr(instr[31:7]), .Immsel(Immsel), .Imm(imm_1_imm));
  Multiplier #(.width(32)) multiplier_1 (.a(register_2_q), .b(32'h4), .out(multiplier_1_out));  // open: cin, cout
  regfile_main main_1 (
    .rs2(instr[24:20]), .rd(instr[11:7]), .Read_Data_1(main_1_read_data_1), .Read_Data_2(main_1_read_data_2),
    .ra(ra), .sp(sp), .t0(t0), .t1(t1), .t2(t2), .s0(s0), .s1(s1), .a0(a0), .rs1(instr[19:15]),
    .Write_Data(multiplexer_6_out), .RegWEn(RegWEn), .clk(CLOCK));
  Multiplexer #(.width(32), .enable("false")) multiplexer_3 (
    .in0(main_1_read_data_2), .in1(imm_1_imm), .out(multiplexer_3_out), .sel(BSel));
  Multiplexer #(.width(32), .enable("false")) multiplexer_4 (
    .in0(main_1_read_data_1), .in1(multiplier_1_out), .out(multiplexer_4_out), .sel(ASel));
  alu alu_1 (.A(multiplexer_4_out), .B(multiplexer_3_out), .ALUSel(ALUSel), .Result(alu_1_result));
  cmp cmp_1 (.A(main_1_read_data_1), .B(main_1_read_data_2), .BrUn(BrUn), .BrEq(BEQ), .BrLT(BLT));
  assign bit_extender_1_out = {{24{load_data[7]}}, load_data[7:0]};  // Bit_Extender bit_extender_1
  assign bit_extender_2_out = {{16{load_data[15]}}, load_data[15:0]};  // Bit_Extender bit_extender_2
  assign bit_extender_3_out = {{24{1'b0}}, load_data[7:0]};  // Bit_Extender bit_extender_3
  assign bit_extender_4_out = {{16{1'b0}}, load_data[15:0]};  // Bit_Extender bit_extender_4
  mem_main main_2 (
    .WriteAddr(alu_1_result), .WriteData(main_1_read_data_2), .MemRW(MemRW), .ReadData(load_data), .clk(CLOCK));
  Multiplexer #(.select(3), .width(32), .enable("false")) multiplexer_5 (
    .in0(bit_extender_1_out), .in1(bit_extender_2_out), .in2(load_data), .in4(bit_extender_3_out),
    .in5(bit_extender_4_out), .out(load_done), .sel(data_size));  // open: in3, in6, in7
  Multiplexer #(.select(2), .width(32), .enable("false")) multiplexer_6 (
    .in0(load_done), .in1(alu_1_result), .in2(adder_2_out), .out(multiplexer_6_out), .sel(WBSel));  // open: in3

  // Other names for the same wires on the sheet: clk = CLOCK; fetch_addr[31:0] = FETCH_ADDRESS

  // Notes on the sheet:
  //   Output
  //   Inputs/Outputs from run.circ. DO NOT MOVE THESE.
  //   Inputs
  //   Inputs/Outputs from run.circ. DO NOT MOVE THESE.
endmodule

module Control (
  input  [31:0] in_1,
  input  BrEq,
  input  BrLT,
  output [2:0] ImmSel,
  output BrUn,
  output Asel,
  output Bsel,
  output [3:0] ALUSel,
  output MemRW,
  output RegWEn,
  output [1:0] WBSel,
  output PCSel,
  output [2:0] data_size
);

  wire and_1_out, and_2_out, and_3_out, and_4_out, and_5_out, comparator_1_eq, comparator_2_eq,
       comparator_3_eq, comparator_4_eq, comparator_5_eq, comparator_6_eq, comparator_7_eq, comparator_8_eq,
       comparator_9_eq, comparator_10_eq, comparator_11_eq, comparator_12_eq, comparator_13_eq,
       comparator_14_eq, comparator_15_eq, comparator_16_eq, comparator_17_eq, comparator_18_eq,
       comparator_19_eq, comparator_20_eq, multiplexer_6_out, not_1_out, not_2_out, or_1_out, or_2_out,
       or_3_out, or_4_out, PCSel_1;
  wire [0:0] rom_1_data;
  wire [1:0] adder_1_out, bit_extender_9_out, bit_extender_10_out, bit_extender_11_out, funct7_ret,
       funct7_sel, multiplexer_1_out, multiplier_9_out, multiplier_10_out, multiplier_11_out;
  wire [2:0] adder_2_out, adder_3_out, adder_4_out, adder_5_out, adder_7_out, adder_8_out,
       bit_extender_1_out, bit_extender_2_out, bit_extender_3_out, bit_extender_4_out, bit_extender_5_out,
       bit_extender_6_out, bit_extender_7_out, bit_extender_8_out, multiplier_1_out, multiplier_2_out,
       multiplier_3_out, multiplier_4_out, multiplier_5_out, multiplier_6_out, multiplier_7_out,
       multiplier_8_out, op_sel;
  wire [7:0] multiplexer_3_out, multiplexer_4_out;

  Comparator #(.width(7), .mode("unsigned")) comparator_1 (
    .a(in_1[6:0]), .b(7'b0110011), .eq(comparator_1_eq));  // open: gt, lt
  Comparator #(.width(7), .mode("unsigned")) comparator_2 (
    .a(in_1[6:0]), .b(7'b0000011), .eq(comparator_2_eq));  // open: gt, lt
  Comparator #(.width(7), .mode("unsigned")) comparator_3 (
    .a(in_1[6:0]), .b(7'b0010011), .eq(comparator_3_eq));  // open: gt, lt
  Comparator #(.width(7), .mode("unsigned")) comparator_4 (
    .a(in_1[6:0]), .b(7'b0100011), .eq(comparator_4_eq));  // open: gt, lt
  Comparator #(.width(7), .mode("unsigned")) comparator_5 (
    .a(in_1[6:0]), .b(7'b1100011), .eq(comparator_5_eq));  // open: gt, lt
  Comparator #(.width(7), .mode("unsigned")) comparator_6 (
    .a(in_1[6:0]), .b(7'b0110111), .eq(comparator_6_eq));  // open: gt, lt
  Comparator #(.width(7), .mode("unsigned")) comparator_7 (
    .a(in_1[6:0]), .b(7'b1101111), .eq(comparator_7_eq));  // open: gt, lt
  Comparator #(.width(7), .mode("unsigned")) comparator_8 (
    .a(in_1[6:0]), .b(7'b1100111), .eq(comparator_8_eq));  // open: gt, lt
  Comparator #(.width(7), .mode("unsigned")) comparator_9 (
    .a(in_1[31:25]), .b({7{1'b0}}), .eq(comparator_9_eq));  // open: gt, lt
  Comparator #(.width(7), .mode("unsigned")) comparator_10 (
    .a(in_1[31:25]), .b(7'b0000001), .eq(comparator_10_eq));  // open: gt, lt
  Comparator #(.width(7), .mode("unsigned")) comparator_11 (
    .a(in_1[31:25]), .b(7'b0100000), .eq(comparator_11_eq));  // open: gt, lt
  assign bit_extender_1_out = {{2{1'b0}}, comparator_1_eq};  // Bit_Extender bit_extender_1
  assign bit_extender_2_out = {{2{1'b0}}, comparator_2_eq};  // Bit_Extender bit_extender_2
  assign bit_extender_3_out = {{2{1'b0}}, comparator_3_eq};  // Bit_Extender bit_extender_3
  assign bit_extender_4_out = {{2{1'b0}}, comparator_4_eq};  // Bit_Extender bit_extender_4
  assign bit_extender_5_out = {{2{1'b0}}, comparator_5_eq};  // Bit_Extender bit_extender_5
  assign bit_extender_6_out = {{2{1'b0}}, comparator_6_eq};  // Bit_Extender bit_extender_6
  assign bit_extender_7_out = {{2{1'b0}}, comparator_7_eq};  // Bit_Extender bit_extender_7
  assign bit_extender_8_out = {{2{1'b0}}, comparator_8_eq};  // Bit_Extender bit_extender_8
  assign bit_extender_9_out = {{1{1'b0}}, comparator_9_eq};  // Bit_Extender bit_extender_9
  assign bit_extender_10_out = {{1{1'b0}}, comparator_10_eq};  // Bit_Extender bit_extender_10
  assign bit_extender_11_out = {{1{1'b0}}, comparator_11_eq};  // Bit_Extender bit_extender_11
  Multiplier #(.width(3)) multiplier_1 (.a(bit_extender_1_out), .b(3'b000), .out(multiplier_1_out));  // open: cin, cout
  Multiplier #(.width(3)) multiplier_2 (.a(bit_extender_2_out), .b(3'b001), .out(multiplier_2_out));  // open: cin, cout
  Multiplier #(.width(3)) multiplier_3 (.a(bit_extender_3_out), .b(3'b010), .out(multiplier_3_out));  // open: cin, cout
  Multiplier #(.width(3)) multiplier_4 (.a(bit_extender_4_out), .b(3'b011), .out(multiplier_4_out));  // open: cin, cout
  Multiplier #(.width(3)) multiplier_5 (.a(bit_extender_5_out), .b(3'b100), .out(multiplier_5_out));  // open: cin, cout
  Multiplier #(.width(3)) multiplier_6 (.a(bit_extender_6_out), .b(3'b101), .out(multiplier_6_out));  // open: cin, cout
  Multiplier #(.width(3)) multiplier_7 (.a(bit_extender_7_out), .b(3'b110), .out(multiplier_7_out));  // open: cin, cout
  Multiplier #(.width(3)) multiplier_8 (.a(bit_extender_8_out), .b(3'b111), .out(multiplier_8_out));  // open: cin, cout
  Multiplier #(.width(2)) multiplier_9 (.a(2'b01), .b(bit_extender_9_out), .out(multiplier_9_out));  // open: cin, cout
  Multiplier #(.width(2)) multiplier_10 (
    .a(2'b10), .b(bit_extender_10_out), .out(multiplier_10_out));  // open: cin, cout
  Multiplier #(.width(2)) multiplier_11 (
    .a(2'b11), .b(bit_extender_11_out), .out(multiplier_11_out));  // open: cin, cout
  Adder #(.width(2)) adder_1 (.a(multiplier_9_out), .b(multiplier_10_out), .out(adder_1_out));  // open: cin, cout
  Adder #(.width(3)) adder_2 (.a(multiplier_1_out), .b(multiplier_2_out), .out(adder_2_out));  // open: cin, cout
  Adder #(.width(3)) adder_3 (.a(multiplier_3_out), .b(multiplier_4_out), .out(adder_3_out));  // open: cin, cout
  Adder #(.width(3)) adder_4 (.a(multiplier_5_out), .b(multiplier_6_out), .out(adder_4_out));  // open: cin, cout
  Adder #(.width(3)) adder_5 (.a(multiplier_7_out), .b(multiplier_8_out), .out(adder_5_out));  // open: cin, cout
  Adder #(.width(2)) adder_6 (.a(adder_1_out), .b(multiplier_11_out), .out(funct7_sel));  // open: cin, cout
  Adder #(.width(3)) adder_7 (.a(adder_2_out), .b(adder_3_out), .out(adder_7_out));  // open: cin, cout
  Adder #(.width(3)) adder_8 (.a(adder_4_out), .b(adder_5_out), .out(adder_8_out));  // open: cin, cout
  Adder #(.width(3)) adder_9 (.a(adder_7_out), .b(adder_8_out), .out(op_sel));  // open: cin, cout
  Multiplexer #(.select(3), .width(2), .enable("false")) multiplexer_1 (
    .in0(2'b00), .in1(funct7_sel), .in2(2'b00), .in3(2'b00), .in4(2'b00), .in5(funct7_sel), .in6(2'b00),
    .in7(2'b00), .out(multiplexer_1_out), .sel(in_1[14:12]));
  Comparator #(.width(3), .mode("unsigned")) comparator_12 (
    .a(op_sel), .b(3'b010), .eq(comparator_12_eq));  // open: gt, lt
  Multiplexer #(.width(2), .enable("false")) multiplexer_2 (
    .in0(funct7_sel), .in1(multiplexer_1_out), .out(funct7_ret), .sel(comparator_12_eq));
  Multiplexer #(.select(3), .width(8), .enable("false")) multiplexer_3 (
    .in0({op_sel, in_1[14:12], funct7_ret}), .in1({op_sel, in_1[14:12], 2'b00}),
    .in2({op_sel, in_1[14:12], funct7_ret}), .in3({op_sel, {5{1'b0}}}), .in4({op_sel, in_1[14:12], 2'b00}),
    .in5({op_sel, {5{1'b0}}}), .in6({op_sel, {5{1'b0}}}), .in7({op_sel, {5{1'b0}}}), .out(multiplexer_3_out),
    .sel(op_sel));
  Comparator #(.width(7), .mode("unsigned")) comparator_13 (
    .a(in_1[6:0]), .b(7'b0010111), .eq(comparator_13_eq));  // open: gt, lt
  Multiplexer #(.width(8), .enable("false")) multiplexer_4 (
    .in0(multiplexer_3_out), .in1(8'hf0), .out(multiplexer_4_out), .sel(comparator_13_eq));
  Comparator #(.width(3), .mode("unsigned")) comparator_14 (
    .a(in_1[14:12]), .b(3'b000), .eq(comparator_14_eq));  // open: gt, lt
  Comparator #(.width(3), .mode("unsigned")) comparator_15 (
    .a(in_1[14:12]), .b(3'b100), .eq(comparator_15_eq));  // open: gt, lt
  Comparator #(.width(3), .mode("unsigned")) comparator_16 (
    .a(in_1[14:12]), .b(3'b110), .eq(comparator_16_eq));  // open: gt, lt
  Comparator #(.width(3), .mode("unsigned")) comparator_17 (
    .a(in_1[14:12]), .b(3'b001), .eq(comparator_17_eq));  // open: gt, lt
  not not_1 (not_1_out, BrEq);
  Comparator #(.width(3), .mode("unsigned")) comparator_18 (
    .a(in_1[14:12]), .b(3'b111), .eq(comparator_18_eq));  // open: gt, lt
  not not_2 (not_2_out, BrLT);
  and and_1 (and_1_out, comparator_14_eq, BrEq);
  and and_2 (and_2_out, comparator_15_eq, BrLT);
  and and_3 (and_3_out, comparator_16_eq, BrLT);
  and and_4 (and_4_out, comparator_17_eq, not_1_out);
  and and_5 (and_5_out, comparator_18_eq, not_2_out);
  Multiplexer #(.width(3), .enable("false")) multiplexer_5 (
    .in0(3'b010), .in1(in_1[14:12]), .out(data_size), .sel(comparator_19_eq));
  Comparator #(.width(7), .mode("unsigned")) comparator_19 (
    .a(in_1[6:0]), .b(7'b0000011), .eq(comparator_19_eq));  // open: gt, lt
  or or_1 (or_1_out, and_1_out, and_2_out);
  or or_2 (or_2_out, and_3_out, and_4_out);
  ROM #(.dataWidth(16)) rom_1 (
    .addr(multiplexer_4_out),
    .data({PCSel_1, ImmSel, BrUn, Asel, Bsel, ALUSel, MemRW, RegWEn, WBSel, rom_1_data[0]}));
  or or_3 (or_3_out, or_1_out, or_2_out);
  or or_4 (or_4_out, or_3_out, and_5_out);
  Multiplexer #(.enable("false")) multiplexer_6 (.in0(1'b0), .in1(1'b1), .out(multiplexer_6_out), .sel(or_4_out));
  Comparator #(.width(3), .mode("unsigned")) comparator_20 (
    .a(op_sel), .b(3'b100), .eq(comparator_20_eq));  // open: gt, lt
  Multiplexer #(.enable("false")) multiplexer_7 (
    .in0(PCSel_1), .in1(multiplexer_6_out), .out(PCSel), .sel(comparator_20_eq));

  // Other names for the same wires on the sheet: funct3[2:0] = in_1[14:12]; opcode[6:0] = in_1[6:0];
  //   funct7[6:0] = in_1[31:25]

  // Notes on the sheet:
  //   0110011->0
  //   0000011->1
  //   0010011->2
  //   0100011->3
  //   1100011->4
  //   0110111->5
  //   1101111->6
  //   1100111->7
  //   0000000->0
  //   0000001->1
  //   0100000->2
  //   instr
  //   auipc 0x17
  //   234
  //   funct3 0-7
  //   01
  //   567
  //   contents of rom_1 (hex, n*v repeats v):
  //   0 a 14a 18a 0 ca 1ca 7*0 16a 0 0 6a 0 0 0 8a 10a 0 0 4a 0 0 0 2a 12a 0 208 0 0 0 208 0 0 0 208 0 0 0
  //   208 0 0 0 208 0 0 0 208 0 0 0 208 7*0 20a 20a 0 0 2ca 2ca 0 0 2ea 2ea 6*0 26a 26a 0 0 28a 28a 0 2aa
  //   24a 24a 0 0 22a 0 0 0 1210 31*0 2600 0 0 0 2600 11*0 a600 7*0 ae00 0 0 0 ae00 0 0 0 33ea 31*0 c60c
  //   31*0 820c 15*0 360a
endmodule

module Imm (
  input  [24:0] instr,
  input  [2:0] Immsel,
  output [31:0] Imm
);

  wire [31:0] Btype, Itype, Jtype, Stype;

  assign Itype = {{20{instr[24]}}, instr[24:13]};  // Bit_Extender bit_extender_1
  assign Stype = {{20{instr[24]}}, {instr[24:18], instr[4:0]}};  // Bit_Extender bit_extender_2
  assign Btype = {{19{instr[24]}}, {instr[24], instr[0], instr[23:18], instr[4:1], 1'b0}};  // Bit_Extender bit_extender_3
  assign Jtype = {{11{instr[24]}}, {instr[24], instr[12:5], instr[13], instr[23:14], 1'b0}};  // Bit_Extender bit_extender_4
  Multiplexer #(.select(3), .width(32), .enable("false")) multiplexer_1 (
    .in0(Itype), .in1(Stype), .in2(Btype), .in3({instr[24:5], {12{1'b0}}}), .in4(Jtype), .out(Imm),
    .sel(Immsel));  // open: in5, in6, in7

  // Other names for the same wires on the sheet: S8to11[3:0] = instr[4:1]; S7 = instr[0]; S21to24[3:0] = instr[17:14];
  //   Utype[31:12] = instr[24:5]; S25to30[5:0] = instr[23:18]; S20 = instr[13]; S12to19[7:0] = instr[12:5];
  //   S31 = instr[24]
endmodule

module cmp (
  input  [31:0] A,
  input  [31:0] B,
  input  BrUn,
  output BrEq,
  output BrLT
);

  wire comparator_1_eq, comparator_1_lt, comparator_2_eq, comparator_2_lt;

  Comparator #(.width(32)) comparator_1 (.a(A), .b(B), .eq(comparator_1_eq), .lt(comparator_1_lt));  // open: gt
  Comparator #(.width(32), .mode("unsigned")) comparator_2 (
    .a(A), .b(B), .eq(comparator_2_eq), .lt(comparator_2_lt));  // open: gt
  Multiplexer #(.enable("false")) multiplexer_1 (.in0(comparator_1_eq), .in1(comparator_2_eq), .out(BrEq), .sel(BrUn));
  Multiplexer #(.enable("false")) multiplexer_2 (.in0(comparator_1_lt), .in1(comparator_2_lt), .out(BrLT), .sel(BrUn));
endmodule
